# Fritzing sketch ESP32-Project (saved by Fritzing 0.9.3b)
breadboards: 1

parts:
  U2 = ESP32S-HiLetgo [part_number=ESP32S-HiLetgo]
  DHT1 = DHT22 Humidity and Temperature Sensor
  Capacitive_Soil_Moisture_Sensor1 = DFRobot Capacitive Soil Moisture Sensor V1.0 [part_number=SEN0193]  # not connected
  Componente1 = Solid State High Level Relay Module [package=relay]
  VALVE1 = Plastic Solenoid Valve
  hc-sr1 = hc-sr04  # not connected
  LED2 = RGB LED (com. cathode, rgb) [package="5 mm [THT]"]
  Power_plug1 = Power plug
  Power_plug2 = Power plug

nets:
  N1: U2.GPIO33, DHT1.DATA
  N2: U2.GPIO27, LED2.blue_anode
  N3: U2.GPIO14, LED2.green_anode
  N4: U2.GPIO12, LED2.red_anode
  VDD: DHT1.VDD, Power_plug1.VCC
  GND: DHT1.GND, LED2.common_cathode, Power_plug1.GND
  N5: Componente1.DC+, Power_plug2.VCC
  N6: Componente1.A1, VALVE1.no_name_yet
  N7: Componente1.DC-, Power_plug2.GND

custom parts:
  ESP32S-HiLetgo: HiLetgo ESP-WROOM-32 ESP32 ESP-32S Development Board 2.4GHz Dual-Mode WiFi + Bluetooth Dual Cores Microcontroller The ESP32 integrated with Antenna switches, RF Balun, power amplifiers, low-noise amplifiers, filters, and management modules, and the entire solution occupies the least area of PCB. 2.4 GHz Wi-Fi plus Bluetooth dual-mode chip, with TSMC Ultra-low power consumption 40nm technology,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
  DFRobot Capacitive Soil Moisture Sensor V1.0: DFRobot Capacitive Soil Moisture Sensor V1.0 This product measures soil moisture levels by capacitive sensing, rather than resistive sensing like other types of moisture sensor. It is made of a corrosion resistant material giving it a long service life. Insert it into soil and impress your friends with the real-time soil moisture data! The product includes an on-board voltage regulator which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
  Solid State High Level Relay Module: 5V Omron solid state relay 240V 2A output with resistance fuse.
